# Fritzing sketch SkateDriver (saved by Fritzing 0.9.3b)
stripboards: 2
perfboards: 2

parts:
  元件1 = Arduino Uno (Rev3)
  元件2 = Bluetooth HC-05 Macho
  VCC1 = Battery
  元件3 = Arduino Nano (Rev3.0)  # not connected
  JP1 = M16 [package=1x16_machine-pin-header_lock.004]  # not connected
  JP2 = M16 [package=1x16_machine-pin-header_lock.004]  # not connected

nets:
  N1: 元件1.D2, 元件2.TXD
  N2: 元件1.D4, 元件2.RXD
  GND: 元件1.GND, 元件2.GND, VCC1.-
  N3: 元件2.VCC, VCC1.+
